# Fritzing sketch Meteo_V2 (saved by Fritzing 0.9.3b)
circuit board: 8.46667cm x 5.64444cm
breadboards: 1

parts:
  Composant2 = Memoire 1.0 - SD card log shield
  Composant3 = Real Time Clock Module - DS1307 RTC Breakout Board
  J1 = RJ11 Jack [package=rj11-6]
  C1 = Ceramic Capacitor [capacitance=100nF package="100 mil [THT, multilayer]"]

nets:
  GND: Composant2.GND, Composant3.GND, Composant3.SDA, J1.4, C1.1
  N1: Composant2.AREF, Composant3.SCL
  N2: Composant2.DIG_2, J1.5, C1.0
  +5V: Composant2.+5V, Composant3.5V

custom parts:
  Real Time Clock Module - DS1307 RTC Breakout Board: This a custom designed module for the DS1307 Real Time Clock. The module comes fully assembled and pre-programmed with the current time (ok, so it's our current time - MST). The included Lithium coin cell battery (CR1225 41mAh) will run the module for a minimum of 9 years (17 years typical) without external 5V power. The DS1307 is accessed via the I2C protocol. We've written a test-bed to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
